# Fritzing sketch Pots (saved by Fritzing 0.9.3b)

parts:
  R1 = Rotary Potentiometer (Small) [maximum_resistance=100kΩ package=THT]
  Част1 = Arduino Uno (Rev3)
  R2 = Rotary Potentiometer (Small) [maximum_resistance=100kΩ package=THT]
  R3 = Rotary Potentiometer (Small) [maximum_resistance=100kΩ package=THT]
  R4 = Rotary Potentiometer (Small) [maximum_resistance=100kΩ package=THT]

nets:
  N1: R1.leg1, Част1.GND, R2.leg1, R3.leg1, R4.leg1
  N2: R1.wiper, Част1.A0
  N3: R1.leg2, Част1.AREF, R2.leg2, R3.leg2, R4.leg2
  N4: Част1.A1, R4.wiper
  N5: Част1.A2, R2.wiper
  N6: Част1.A3, R3.wiper

notes:
  RC Controller +V
  RC Controller GND
